# Fritzing sketch lightsaber (saved by Fritzing 0.9.2b)

parts:
  S1 = Pushbutton [package="[SMD]"]
  S2 = Pushbutton [package="[SMD]"]
  IC1 = SO08 [chip_label="Lipoly Backpack" package=SO]
  U1 = LIPO-2000mAh [package=lipo-2000]
  S3 = Pushbutton [package=THT]
  NEOPIXEL1 = Neopixel Strip -- Black (30/m)
  IC2 = IC, DIP package, 16 pins [chip_label=JQ6500-16p]
  SP1 = SPEAKER [package=pcb_mount_speaker]
  Part1 = Pro Trinket 5V
  S4 = Pushbutton [package="[SMD]"]  # not connected
  S5 = Tilt Switch [package=THT]

nets:
  N1: S1.Pin_3, S1.Pin_4, S2.Pin_2, IC1.2, IC2.pin6, Part1.GND, Part1.D10, S5.Pin_1
  N2: S2.Pin_3, S2.Pin_4, Part1.D9
  N3: IC1.1, Part1.VBAT
  N4: IC1.3, Part1.VBUS
  N5: IC1.5, S3.leg0
  N6: IC1.6, S3.leg1
  N7: IC1.7, U1.+, NEOPIXEL1.+5V, IC2.pin12
  N8: IC1.8, U1.-, NEOPIXEL1.GND
  N9: NEOPIXEL1.Din, Part1.D13
  N10: IC2.pin9, Part1.D5
  N11: IC2.pin10, Part1.D4
  N12: IC2.pin15, SP1.-
  N13: IC2.pin16, SP1.+
  N14: Part1.D11, S5.Pin_2

notes:
  This is adafruit's lipoly backpack add-on (part id 2124)
  Using a 5V trinket so the digital output can drive directly the 5V NeoPixel. Maybe things would also work with the 3V version.

custom parts:
  Neopixel Strip -- Black (30/m): These NeoPixel strips have 30 digitally-addressable pixel LEDs per meter and are very affordable and are only 12.5 mm wide, 10 mm if you remove the strip from the casing.
  Pro Trinket 5V: The Pro Trinket 5V is like an Arduino Pro Mini with more pins and USB included. Built with the common core Arduino chip, the ATmega328p, it has 18 GPIO, 2 extra analog inputs, 28K of flash, and 2K of RAM. It has onboard USB bootloading support with Optiboot support, so you can either program your Pro Trinket over USB or with a FTDI cable. The Pro Trinket is programmable using the Arduino IDE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
